# Fritzing sketch CircuitBoard (saved by Fritzing 0.9.3b)
circuit board: 4.97182cm x 5.33401cm
breadboards: 1

parts:
  Part1 = Arduino Uno (Rev3)
  SD = MicroSD Breakout
  Accelerometer = Adafruit ADXL335 [part_number="Adafruit #163"]
  RTC = DS1307 RTC Breakout
  Altimeter = TCS34725 RGB Color Sensor

nets:
  N1: Part1.A0, Accelerometer.ZOUT
  N2: Part1.A1, Accelerometer.YOUT
  N3: Part1.A2, Accelerometer.XOUT
  N4: Part1.A4/SDA, RTC.SDA, Altimeter.VDD
  N5: Part1.A5/SCL, RTC.SCL, Altimeter.GND
  N6: Part1.D10_PWM/SS, SD.CS
  N7: Part1.D11_PWM/MOSI, SD.DI
  N8: Part1.D12/MISO, SD.DO
  N9: Part1.D13/SCK, SD.CLK
  GND: Part1.GND, SD.GND, Accelerometer.GND, RTC.GND, Altimeter.INT
  5V: Part1.5V, SD.5V, Accelerometer.VIN, RTC.5V, Altimeter.LED

custom parts:
  MicroSD Breakout: 5V-ready microSD Breakout with Level Shifter
  Adafruit ADXL335: We've updated our favorite triple-axis accelerometer to now have an on-board 3.3V regulator - making it a perfect choice for interfacing with a 5V microcontroller such as the Arduino. This breakout comes with 3 analog outputs for X, Y and Z axis measurements on a 0.75"x0.75" breakout board. The ADXL335 is the latest and greatest from Analog Devices, known for their exceptional quality MEMS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
  DS1307 RTC Breakout: DS1307 Real-time Clock Breakout Board with Battery
  TCS34725 RGB Color Sensor: TCS34725 RGB Color Sensor with LED
